// Logisim project TRABALHO DE ARQUITETURA DE COMPUTADORES CC3MB.circ as structural Verilog: 3 circuits, main circuit main
module main (
  input  in_1,
  input  in_2,
  input  in_3,
  output out_4,
  output out_5
);

  ADD_1 add_1_1 (.A(in_1), .B(in_2), .VEM_1(in_3), .S(out_5), .VAI_1(out_4));
endmodule

module ADD_1 (
  input  A,
  input  B,
  input  VEM_1,
  output S,
  output VAI_1
);

  wire and_1_out, and_2_out, or_1_out, xor_1_out;

  xor xor_1 (xor_1_out, A, B);
  or or_1 (or_1_out, B, VEM_1);
  and and_1 (and_1_out, B, VEM_1);
  xor xor_2 (S, xor_1_out, VEM_1);
  and and_2 (and_2_out, or_1_out, A);
  or or_2 (VAI_1, and_2_out, and_1_out);
endmodule

module ADD_4 (
  input  [3:0] in_1,
  input  [3:0] in_2,
  input  VEM_1,
  output VAI_1,
  output [3:0] out_5
);

  wire add_1_2_vai_1, add_1_3_vai_1, add_1_4_vai_1;

  ADD_1 add_1_1 (.A(in_1[3]), .B(in_2[3]), .VEM_1(add_1_2_vai_1), .S(out_5[3]), .VAI_1(VAI_1));
  ADD_1 add_1_2 (.A(in_1[2]), .B(in_2[2]), .VEM_1(add_1_3_vai_1), .S(out_5[2]), .VAI_1(add_1_2_vai_1));
  ADD_1 add_1_3 (.A(in_1[1]), .B(in_2[1]), .VEM_1(add_1_4_vai_1), .S(out_5[1]), .VAI_1(add_1_3_vai_1));
  ADD_1 add_1_4 (.A(in_1[0]), .B(in_2[0]), .VEM_1(VEM_1), .S(out_5[0]), .VAI_1(add_1_4_vai_1));
endmodule
